// Logisim project Real_Alu.circ as structural Verilog
module Mux_4bit (
  input  S3,
  input  S2,
  input  S1,
  input  S0,
  input  _0,
  input  _1,
  input  _2,
  input  _3,
  input  _4,
  input  _5,
  input  _6,
  input  _7,
  input  _8,
  input  _9,
  input  _10,
  input  _11,
  input  _12,
  input  _13,
  input  _14,
  input  _15,
  output out_21
);

  wire _0_t, _1_t, _2_t, _3_t, _4_t, _5_t, _6_t, _7_t, _8_t, _9_t, _10_t, _11_t, _12_t, _13_t, _14_t, _15_t,
       S00, S11, S22, S33;

  not not_1 (S22, S2);
  not not_2 (S33, S3);
  not not_3 (S00, S0);
  not not_4 (S11, S1);
  and and_1 (_0_t, S00, S11, S22, S33, _0);
  and and_2 (_1_t, S0, S11, S22, S33, _1);
  and and_3 (_2_t, S00, S1, S22, S33, _2);
  and and_4 (_3_t, S0, S1, S22, S33, _3);
  and and_5 (_4_t, S00, S11, S2, S33, _4);
  and and_6 (_5_t, S0, S11, S2, S33, _5);
  and and_7 (_6_t, S00, S1, S2, S33, _6);
  and and_8 (_7_t, S0, S1, S2, S33, _7);
  and and_9 (_8_t, S00, S11, S22, S3, _8);
  and and_10 (_9_t, S0, S11, S22, S3, _9);
  and and_11 (_10_t, S00, S1, S22, S3, _10);
  and and_12 (_11_t, S0, S1, S22, S3, _11);
  and and_13 (_12_t, S00, S11, S2, S3, _12);
  and and_14 (_13_t, S0, S11, S2, S3, _13);
  and and_15 (_14_t, S00, S1, S2, S3, _14);
  and and_16 (_15_t, S0, S1, S2, S3, _15);
  or or_1 (out_21, _0_t, _1_t, _2_t, _3_t, _4_t, _5_t, _6_t, _7_t, _8_t, _9_t, _10_t, _11_t, _12_t, _13_t, _14_t, _15_t);
endmodule

module And (
  input  [7:0] a,
  input  [7:0] b,
  output [7:0] out_3,
  output out_4
);

  assign out_3 = a & b;  // AND_Gate and_1, 8 bits wide
  nor nor_1 (out_4, out_3[7], out_3[6], out_3[5], out_3[4], out_3[3], out_3[2], out_3[1], out_3[0]);
endmodule

module Or (
  input  [7:0] a,
  input  [7:0] b,
  output [7:0] out_3,
  output z
);

  assign out_3 = a | b;  // OR_Gate or_1, 8 bits wide
  nor nor_1 (z, out_3[7], out_3[6], out_3[5], out_3[4], out_3[3], out_3[2], out_3[1], out_3[0]);
endmodule

module Not_B (
  input  [7:0] B,
  output [7:0] out_2,
  output z
);

  assign out_2 = ~B;  // NOT_Gate not_1, 8 bits wide
  nor nor_1 (z, out_2[7], out_2[6], out_2[5], out_2[4], out_2[3], out_2[2], out_2[1], out_2[0]);
endmodule

module LSR_B (
  input  [7:0] B,
  output [7:0] out_2,
  output Carry,
  output Z,
  output P_N
);

  nor nor_1 (Z, B[0], B[1], B[2], B[3], B[4], B[5], B[6], B[7]);

  assign Carry = B[7];
  assign out_2 = {B[6:0], 1'b0};
  assign P_N = B[7];
endmodule

module LSL_B (
  input  [7:0] B,
  output Carry,
  output [7:0] out_3,
  output Z,
  output P_N
);

  nor nor_1 (Z, B[0], B[1], B[2], B[3], B[4], B[5], B[6], B[7]);

  assign Carry = B[0];
  assign out_3 = {1'b0, B[7:1]};
  assign P_N = B[7];
endmodule
